# Fritzing sketch brain (saved by Fritzing 0.8.0b)
breadboards: 1

parts:
  C2 = Ceramic Capacitor [package="100 mil [THT, multilayer]"]
  C3 = Ceramic Capacitor [package="100 mil [THT, multilayer]"]
  XTAL1 = Crystal [frequency="16 Mhz" package=THT]
  R1 = Resistor [tolerance=±5% resistance=220 package=THT]
  C4 = Electrolytic Capacitor [capacitance=47µF package="100 mil [THT, electrolytic]"]
  LED1 = LED - 3mm [color="Green (555nm)" package="3 mm [THT]"]
  J3 = double row male pin header, 6 pins [form="♂ (male)"]
  J4 = female pin header, 4 pins [form="♀ (female)"]
  J2 = rounded female pin header, 6 pins [form="♀ (female rounded)"]
  J5 = rounded female pin header, 5 pins [form="♀ (female rounded)"]
  IC1 = IC, DIP package, 14 pins [chip_label=ATTiny84]

nets:
  GND: C2.0, C3.0, C4.-, LED1.cathode, J3.pin4, J4.pin1, J2.pin6, J5.pin2, IC1.pin14
  N1: C2.1, XTAL1.pin_1, IC1.pin2
  N2: C3.1, XTAL1.pin_0, IC1.pin3
  5V: R1.Pin_0, C4.+, J3.pin6, J4.pin2, J2.pin5, J5.pin1, IC1.pin1
  N3: R1.Pin_1, J3.pin3, IC1.pin4
  N4: LED1.anode, IC1.pin5
  N5: J3.pin1, J2.pin3, IC1.pin8
  N6: J3.pin2, J2.pin2, IC1.pin9
  N7: J3.pin5, IC1.pin7
  N8: J4.pin3, IC1.pin6
  12V: J4.pin4, J2.pin4
  N9: J2.pin1, IC1.pin10
  N10: J5.pin3, IC1.pin13
  N11: J5.pin4, IC1.pin12
  N12: J5.pin5, IC1.pin11

notes:
  brain
  woozle.org/derby
  -
  Power Supply
  woozle.org scoreboard, scoreboard brain, 3
  to drivers
  to game pad
  ser
  srck
  rck
  clock
  latch
  serial
  ISP
  black
  yellow
  red
  blue
  Driver
  Game pad
  +5
  C
  L
  S
  12
  E
  +12
  +5V
  NC
  GND

custom parts:
  Ceramic Capacitor: 100 nF multilayer Ceramic Capacitor
