# Fritzing sketch driver (saved by Fritzing 0.8.0b)
breadboards: 1

parts:
  TPIC6B1 = TPIC6B595 [chip_label=TPIC6B595 package="DIP (Dual Inline) [THT]"]
  J3 = female pin header, 4 pins [form="♀ (female)"]
  J6 = female pin header, 4 pins [form="♀ (female)"]
  J1 = female pin header, 6 pins [form="♀ (female)"]
  J4 = female pin header, 6 pins [form="♀ (female)"]
  J7 = female pin header, 2 pins [form="♀ (female)"]
  C1 = Ceramic Capacitor [capacitance=100nF package="100 mil [THT, multilayer]"]

nets:
  5V: TPIC6B1.VCC, TPIC6B1.~SRCLR, J1.pin5, J4.pin5, C1.0
  N1: TPIC6B1.SER_IN, J1.pin1
  N2: TPIC6B1.DRAIN0, J3.pin1
  N3: TPIC6B1.DRAIN1, J3.pin2
  N4: TPIC6B1.DRAIN2, J3.pin3
  N5: TPIC6B1.DRAIN3, J3.pin4
  GND: TPIC6B1.~G, TPIC6B1.GND, J1.pin6, J4.pin6, C1.1
  N6: TPIC6B1.RCK, J1.pin3, J4.pin3
  N7: TPIC6B1.SRCK, J1.pin2, J4.pin2
  N8: TPIC6B1.DRAIN4, J6.pin1
  N9: TPIC6B1.DRAIN5, J6.pin2
  N10: TPIC6B1.DRAIN6, J6.pin3
  N11: TPIC6B1.DRAIN7, J6.pin4
  N12: TPIC6B1.SER_OUT, J4.pin1
  12V: J1.pin4, J4.pin4, J7.pin1, J7.pin2

notes:
  woozle.org/derby
  driver
  in
  out
  +12V
  0-3
  4-7
  woozle.org scoreboard, digit driver, 4
  rck
  srck
  ser
  GND
  +5V
  L
  C
  S
  0
  1
  2
  3
  4
  5
  6
  7

custom parts:
  TPIC6B595: Power Logic 8-bit Shift Register
